// Logisim project Lab4_cuellar.circ as structural Verilog
module ImmGem (
  input  [31:0] Instruction,
  output [31:0] IMM32
);

  Multiplexer #(.enable("false"), .width(4)) multiplexer_1 (
    .in0(Instruction[24:21]), .in1(Instruction[11:8]), .out(IMM32[4:1]), .sel(Instruction[5]));
  Multiplexer #(.enable("false")) multiplexer_2 (
    .in0(Instruction[31]), .in1(Instruction[7]), .out(IMM32[11]), .sel(Instruction[6]));
  assign IMM32[31:12] = {{19{Instruction[31]}}, Instruction[31]};  // Bit_Extender bit_extender_1
  Multiplexer #(.enable("false"), .select(2)) multiplexer_3 (
    .in0(Instruction[20]), .in1(Instruction[7]), .in3(1'b0), .out(IMM32[0]), .sel(Instruction[6:5]));  // open: in2

  assign IMM32[10:5] = Instruction[30:25];

  // Other names for the same wires on the sheet: I30_25[5:0] = Instruction[30:25]; I5 = Instruction[5];
  //   I6_5[1:0] = Instruction[6:5]; I6 = Instruction[6]; I7 = Instruction[7]; I11_8[3:0] = Instruction[11:8];
  //   I20 = Instruction[20]; I24_21[3:0] = Instruction[24:21]; I31 = Instruction[31]
endmodule

module InstructionMemory (
  input  [23:0] Address,
  input  Clockin,
  output [31:0] Instruction
);

  wire not_1_out;

  not not_1 (not_1_out, Clockin);
  RAM #(.addrWidth(22), .asyncread("true"), .dataWidth(32)) ram_1 (
    .addr(Address[23:2]), .we(1'b0), .oe(not_1_out), .dout(Instruction));  // open: clk, din
endmodule

module DataMemory (
  input  [25:0] Address,
  input  MemWrite,
  input  MemRead,
  input  Clockin,
  input  [31:0] WriteData,
  output [31:0] ReadData
);

  RAM #(.addrWidth(24), .asyncread("true"), .dataWidth(32)) ram_1 (
    .addr(Address[25:2]), .we(MemWrite), .oe(MemRead), .clk(Clockin), .din(WriteData), .dout(ReadData));
endmodule

module MainControl (
  input  I6,
  input  I5,
  input  I4,
  input  I3,
  input  I2,
  input  I1,
  input  I0,
  output MemtoReg,
  output RegWrite,
  output MemRead,
  output MemWrite,
  output Branch
);

  wire not_1_out, not_2_out;

  not not_1 (not_1_out, I6);
  not not_2 (not_2_out, I5);
  not not_3 (MemtoReg, I4);
  or or_1 (RegWrite, not_2_out, I4);
  and and_1 (MemRead, not_2_out, MemtoReg);
  and and_2 (MemWrite, not_1_out, I5, MemtoReg);

  assign Branch = I6;
endmodule

module onebitADDER (
  input  A,
  input  B,
  input  Cin,
  output S,
  output Cout
);

  wire and_1_out, and_2_out, and_3_out, and_4_out, and_5_out, and_6_out, and_7_out, not_1_out, not_2_out,
       not_3_out;

  not not_1 (not_1_out, A);
  not not_2 (not_2_out, B);
  not not_3 (not_3_out, Cin);
  and and_1 (and_1_out, not_1_out, not_2_out, Cin);
  and and_2 (and_2_out, not_1_out, B, not_3_out);
  and and_3 (and_3_out, A, not_2_out, not_3_out);
  and and_4 (and_4_out, A, B, Cin);
  and and_5 (and_5_out, B, Cin);
  and and_6 (and_6_out, Cin, A);
  and and_7 (and_7_out, A, B);
  or or_1 (S, and_1_out, and_2_out, and_3_out, and_4_out);
  or or_2 (Cout, and_5_out, and_6_out, and_7_out);
endmodule

module one_bit_ALU (
  input  [3:0] ALU_ctrl,
  input  A,
  input  B,
  input  C_in,
  output R,
  output C_out
);

  wire and_1_out, multiplexer_1_out, not_1_out, onebitadder_1_s, or_1_out, xor_1_out;

  not not_1 (not_1_out, B);
  Multiplexer #(.enable("false")) multiplexer_1 (.in0(B), .in1(not_1_out), .out(multiplexer_1_out), .sel(ALU_ctrl[2]));
  and and_1 (and_1_out, A, multiplexer_1_out);
  or or_1 (or_1_out, A, multiplexer_1_out);
  xor xor_1 (xor_1_out, A, multiplexer_1_out);
  onebitADDER onebitadder_1 (.A(A), .B(multiplexer_1_out), .Cin(C_in), .S(onebitadder_1_s), .Cout(C_out));
  Multiplexer #(.enable("false"), .select(2)) multiplexer_2 (
    .in0(and_1_out), .in1(or_1_out), .in2(xor_1_out), .in3(onebitadder_1_s), .out(R), .sel(ALU_ctrl[1:0]));
endmodule

module ALU_32_bits (
  input  [3:0] ALU_ctrl,
  input  [31:0] A,
  input  [31:0] B,
  output [31:0] R,
  output C_out
);

  wire alu_4_bits_1_c_out, alu_4_bits_2_c_out, alu_4_bits_3_c_out, alu_4_bits_4_c_out, alu_4_bits_5_c_out,
       alu_4_bits_6_c_out, alu_4_bits_7_c_out;

  ALU_4_bits alu_4_bits_1 (
    .ALU_ctrl(ALU_ctrl), .A(A[3:0]), .B(B[3:0]), .C_in(ALU_ctrl[2]), .R(R[3:0]), .C_out(alu_4_bits_1_c_out));
  ALU_4_bits alu_4_bits_2 (
    .ALU_ctrl(ALU_ctrl), .A(A[7:4]), .B(B[7:4]), .C_in(alu_4_bits_1_c_out), .R(R[7:4]),
    .C_out(alu_4_bits_2_c_out));
  ALU_4_bits alu_4_bits_3 (
    .ALU_ctrl(ALU_ctrl), .A(A[11:8]), .B(B[11:8]), .C_in(alu_4_bits_2_c_out), .R(R[11:8]),
    .C_out(alu_4_bits_3_c_out));
  ALU_4_bits alu_4_bits_4 (
    .ALU_ctrl(ALU_ctrl), .A(A[15:12]), .B(B[15:12]), .C_in(alu_4_bits_3_c_out), .R(R[15:12]),
    .C_out(alu_4_bits_4_c_out));
  ALU_4_bits alu_4_bits_5 (
    .ALU_ctrl(ALU_ctrl), .A(A[19:16]), .B(B[23:20]), .C_in(alu_4_bits_4_c_out), .R(R[19:16]),
    .C_out(alu_4_bits_5_c_out));
  ALU_4_bits alu_4_bits_6 (
    .ALU_ctrl(ALU_ctrl), .A(A[23:20]), .B(B[23:20]), .C_in(alu_4_bits_5_c_out), .R(R[23:20]),
    .C_out(alu_4_bits_6_c_out));
  ALU_4_bits alu_4_bits_7 (
    .ALU_ctrl(ALU_ctrl), .A(A[27:24]), .B(B[27:24]), .C_in(alu_4_bits_6_c_out), .R(R[27:24]),
    .C_out(alu_4_bits_7_c_out));
  ALU_4_bits alu_4_bits_8 (
    .ALU_ctrl(ALU_ctrl), .A(A[31:28]), .B(B[31:28]), .C_in(alu_4_bits_7_c_out), .R(R[31:28]), .C_out(C_out));

  assign B[19:16] = B[23:20];
endmodule

module ALU_4_bits (
  input  [3:0] ALU_ctrl,
  input  [3:0] A,
  input  [3:0] B,
  input  C_in,
  output [3:0] R,
  output C_out
);

  wire one_bit_alu_1_c_out, one_bit_alu_2_c_out, one_bit_alu_3_c_out;

  one_bit_ALU one_bit_alu_1 (
    .ALU_ctrl(ALU_ctrl), .A(A[0]), .B(B[0]), .C_in(C_in), .R(R[0]), .C_out(one_bit_alu_1_c_out));
  one_bit_ALU one_bit_alu_2 (
    .ALU_ctrl(ALU_ctrl), .A(A[1]), .B(B[1]), .C_in(one_bit_alu_1_c_out), .R(R[1]), .C_out(one_bit_alu_2_c_out));
  one_bit_ALU one_bit_alu_3 (
    .ALU_ctrl(ALU_ctrl), .A(A[2]), .B(B[2]), .C_in(one_bit_alu_2_c_out), .R(R[2]), .C_out(one_bit_alu_3_c_out));
  one_bit_ALU one_bit_alu_4 (
    .ALU_ctrl(ALU_ctrl), .A(A[3]), .B(B[3]), .C_in(one_bit_alu_3_c_out), .R(R[3]), .C_out(C_out));
endmodule

module register_file_32 (
  input  [31:0] WData,
  input  [4:0] RReg1,
  input  Clock_in,
  input  Write,
  input  [4:0] WReg,
  input  [4:0] RReg2,
  output [31:0] RData1,
  output [31:0] RData2
);

  wire r1, r2, r3, r4, r5, r6, r7, r8, r9, r10, r11, r12, r13, r14, r15, r16, r17, r18, r19, r20, r21, r22,
       r23, r24, r25, r26, r27, r28, r29, r30, r31, r32;
  wire [31:0] Q0, Q1, Q2, Q3, Q4, Q5, Q6, Q7, Q8, Q9, Q10, Q11, Q12, Q13, Q14, Q15, Q16, Q17, Q18, Q19, Q20,
       Q21, Q22, Q23, Q24, Q25, Q26, Q27, Q28, Q29, Q30, Q31;

  Demultiplexer #(.enable("false"), .select(5)) demultiplexer_1 (
    .out0(r1), .out1(r2), .out2(r3), .out3(r4), .out4(r5), .out5(r6), .out6(r7), .out7(r8), .out8(r9),
    .out9(r10), .out10(r11), .out11(r12), .out12(r13), .out13(r14), .out14(r15), .out15(r16), .out16(r17),
    .out17(r18), .out18(r19), .out19(r20), .out20(r21), .out21(r22), .out22(r23), .out23(r24), .out24(r25),
    .out25(r26), .out26(r27), .out27(r28), .out28(r29), .out29(r30), .out30(r31), .out31(r32), .in(Write),
    .sel(WReg));
  Register #(.width(32)) register_1 (.D(WData), .en(r1), .clk(Clock_in), .Q(Q0), .clr(Write));
  Register #(.width(32)) register_2 (.D(WData), .en(r2), .clk(Clock_in), .Q(Q1));  // open: clr
  Register #(.width(32)) register_3 (.D(WData), .en(r3), .clk(Clock_in), .Q(Q2));  // open: clr
  Register #(.width(32)) register_4 (.D(WData), .en(r4), .clk(Clock_in), .Q(Q3));  // open: clr
  Register #(.width(32)) register_5 (.D(WData), .en(r5), .clk(Clock_in), .Q(Q4));  // open: clr
  Register #(.width(32)) register_6 (.D(WData), .en(r6), .clk(Clock_in), .Q(Q5));  // open: clr
  Register #(.width(32)) register_7 (.D(WData), .en(r7), .clk(Clock_in), .Q(Q6));  // open: clr
  Register #(.width(32)) register_8 (.D(WData), .en(r8), .clk(Clock_in), .Q(Q7));  // open: clr
  Register #(.width(32)) register_9 (.D(WData), .en(r9), .clk(Clock_in), .Q(Q8));  // open: clr
  Register #(.width(32)) register_10 (.D(WData), .en(r10), .clk(Clock_in), .Q(Q9));  // open: clr
  Register #(.width(32)) register_11 (.D(WData), .en(r11), .clk(Clock_in), .Q(Q10));  // open: clr
  Register #(.width(32)) register_12 (.D(WData), .en(r12), .clk(Clock_in), .Q(Q11));  // open: clr
  Register #(.width(32)) register_13 (.D(WData), .en(r13), .clk(Clock_in), .Q(Q12));  // open: clr
  Register #(.width(32)) register_14 (.D(WData), .en(r14), .clk(Clock_in), .Q(Q13));  // open: clr
  Register #(.width(32)) register_15 (.D(WData), .en(r15), .clk(Clock_in), .Q(Q14));  // open: clr
  Register #(.width(32)) register_16 (.D(WData), .en(r16), .clk(Clock_in), .Q(Q15));  // open: clr
  Register #(.width(32)) register_17 (.D(WData), .en(r17), .clk(Clock_in), .Q(Q16));  // open: clr
  Register #(.width(32)) register_18 (.D(WData), .en(r18), .clk(Clock_in), .Q(Q17));  // open: clr
  Register #(.width(32)) register_19 (.D(WData), .en(r19), .clk(Clock_in), .Q(Q18));  // open: clr
  Register #(.width(32)) register_20 (.D(WData), .en(r20), .clk(Clock_in), .Q(Q19));  // open: clr
  Register #(.width(32)) register_21 (.D(WData), .en(r21), .clk(Clock_in), .Q(Q20));  // open: clr
  Register #(.width(32)) register_22 (.D(WData), .en(r22), .clk(Clock_in), .Q(Q21));  // open: clr
  Register #(.width(32)) register_23 (.D(WData), .en(r23), .clk(Clock_in), .Q(Q22));  // open: clr
  Register #(.width(32)) register_24 (.D(WData), .en(r24), .clk(Clock_in), .Q(Q23));  // open: clr
  Register #(.width(32)) register_25 (.D(WData), .en(r25), .clk(Clock_in), .Q(Q24));  // open: clr
  Register #(.width(32)) register_26 (.D(WData), .en(r26), .clk(Clock_in), .Q(Q25));  // open: clr
  Register #(.width(32)) register_27 (.D(WData), .en(r27), .clk(Clock_in), .Q(Q26));  // open: clr
  Register #(.width(32)) register_28 (.D(WData), .en(r28), .clk(Clock_in), .Q(Q27));  // open: clr
  Register #(.width(32)) register_29 (.D(WData), .en(r29), .clk(Clock_in), .Q(Q28));  // open: clr
  Register #(.width(32)) register_30 (.D(WData), .en(r30), .clk(Clock_in), .Q(Q29));  // open: clr
  Register #(.width(32)) register_31 (.D(WData), .en(r31), .clk(Clock_in), .Q(Q30));  // open: clr
  Register #(.width(32)) register_32 (.D(WData), .en(r32), .clk(Clock_in), .Q(Q31));  // open: clr
  Multiplexer #(.enable("false"), .select(5), .width(32)) multiplexer_1 (
    .in0(Q0), .in1(Q1), .in2(Q2), .in3(Q3), .in4(Q4), .in5(Q5), .in6(Q6), .in7(Q7), .in8(Q8), .in9(Q9),
    .in10(Q10), .in11(Q11), .in12(Q12), .in13(Q13), .in14(Q14), .in15(Q15), .in16(Q16), .in17(Q17),
    .in18(Q18), .in19(Q19), .in20(Q20), .in21(Q21), .in22(Q22), .in23(Q23), .in24(Q24), .in25(Q25),
    .in26(Q26), .in27(Q27), .in28(Q28), .in29(Q29), .in30(Q30), .in31(Q31), .out(RData1), .sel(RReg1));
  Multiplexer #(.enable("false"), .select(5), .width(32)) multiplexer_2 (
    .in0(Q0), .in1(Q1), .in2(Q2), .in3(Q3), .in4(Q4), .in5(Q5), .in6(Q6), .in7(Q7), .in8(Q8), .in9(Q9),
    .in10(Q10), .in11(Q11), .in12(Q12), .in13(Q13), .in14(Q14), .in15(Q15), .in16(Q16), .in17(Q17),
    .in18(Q18), .in19(Q19), .in20(Q20), .in21(Q21), .in22(Q22), .in23(Q23), .in24(Q24), .in25(Q25),
    .in26(Q26), .in27(Q27), .in28(Q28), .in29(Q29), .in30(Q30), .in31(Q31), .out(RData2), .sel(RReg2));
endmodule

module datapath (
  input  [31:0] Instruction
);

  wire alu_ctrl_1_alu_scr, clock_1_out;
  wire [3:0] alu_ctrl_1_alu_ctrl0;
  wire [31:0] alu_32_bits_1_r, bit_extender_1_out, multiplexer_1_out, register_file_32_1_rdata1,
       register_file_32_1_rdata2;

  Clock clock_1 (.out(clock_1_out));
  assign bit_extender_1_out = {{20{Instruction[31]}}, Instruction[31:20]};  // Bit_Extender bit_extender_1
  register_file_32 register_file_32_1 (
    .WData(alu_32_bits_1_r), .RReg1(Instruction[19:15]), .Clock_in(clock_1_out), .Write(1'b1),
    .WReg(Instruction[11:7]), .RReg2(Instruction[24:20]), .RData1(register_file_32_1_rdata1),
    .RData2(register_file_32_1_rdata2));
  Multiplexer #(.enable("false"), .width(32)) multiplexer_1 (
    .in0(register_file_32_1_rdata2), .in1(bit_extender_1_out), .out(multiplexer_1_out),
    .sel(alu_ctrl_1_alu_scr));
  ALU_ctrl alu_ctrl_1 (
    .I30(Instruction[30]), .I14(Instruction[14]), .I13(Instruction[13]), .I12(Instruction[12]),
    .I6(Instruction[6]), .I5(Instruction[5]), .I4(Instruction[4]), .ALU_ctrl3(alu_ctrl_1_alu_ctrl0[3]),
    .ALU_ctrl2(alu_ctrl_1_alu_ctrl0[2]), .ALU_ctrl1(alu_ctrl_1_alu_ctrl0[1]),
    .ALU_ctrl0(alu_ctrl_1_alu_ctrl0[0]), .ALU_scr(alu_ctrl_1_alu_scr));
  ALU_32_bits alu_32_bits_1 (
    .ALU_ctrl(alu_ctrl_1_alu_ctrl0), .A(register_file_32_1_rdata1), .B(multiplexer_1_out), .R(alu_32_bits_1_r));  // open: C_out
endmodule

module ALU_ctrl (
  input  I30,
  input  I14,
  input  I13,
  input  I12,
  input  I6,
  input  I5,
  input  I4,
  output ALU_ctrl3,
  output ALU_ctrl2,
  output ALU_ctrl1,
  output ALU_ctrl0,
  output ALU_scr
);

  wire and_2_out, not_1_out, not_2_out, not_3_out, not_4_out, not_5_out;

  not not_1 (not_1_out, I14);
  not not_2 (not_2_out, I13);
  not not_3 (not_3_out, I12);
  not not_4 (not_4_out, I5);
  not not_5 (not_5_out, I4);
  and and_1 (ALU_ctrl2, I30, not_2_out, I5);
  buf or_1 (ALU_ctrl1, not_2_out);  // OR_Gate
  and and_2 (and_2_out, I13, not_3_out);
  or or_2 (ALU_scr, not_4_out, not_5_out);
  or or_3 (ALU_ctrl0, not_1_out, and_2_out);

  assign ALU_ctrl3 = 1'b0;
endmodule

module datapath_extracredit (
  input  [31:0] Instruction
);

  wire alu_ctrl_extra_1_alu_src, clock_1_out;
  wire [3:0] alu_ctrl_extra_1_alu_ctrl3;
  wire [31:0] alu_32_bits_1_r, bit_extender_1_out, multiplexer_1_out, register_file_32_1_rdata1,
       register_file_32_1_rdata2;

  Clock clock_1 (.out(clock_1_out));
  assign bit_extender_1_out = {{20{Instruction[31]}}, Instruction[31:20]};  // Bit_Extender bit_extender_1
  register_file_32 register_file_32_1 (
    .WData(alu_32_bits_1_r), .RReg1(Instruction[19:15]), .Clock_in(clock_1_out), .Write(1'b1),
    .WReg(Instruction[11:7]), .RReg2(Instruction[24:20]), .RData1(register_file_32_1_rdata1),
    .RData2(register_file_32_1_rdata2));
  Multiplexer #(.enable("false"), .width(32)) multiplexer_1 (
    .in0(register_file_32_1_rdata2), .in1(bit_extender_1_out), .out(multiplexer_1_out),
    .sel(alu_ctrl_extra_1_alu_src));
  ALU_ctrl_extra alu_ctrl_extra_1 (
    .I30(Instruction[30]), .I14(Instruction[14]), .I13(Instruction[13]), .I12(Instruction[12]),
    .I6(Instruction[6]), .I5(Instruction[5]), .I4(Instruction[4]), .ALU_ctrl3(alu_ctrl_extra_1_alu_ctrl3[0]),
    .ALU_ctrl2(alu_ctrl_extra_1_alu_ctrl3[1]), .ALU_ctrl1(alu_ctrl_extra_1_alu_ctrl3[2]),
    .ALU_ctrl0(alu_ctrl_extra_1_alu_ctrl3[3]), .ALU_Src(alu_ctrl_extra_1_alu_src));
  ALU_32_bits alu_32_bits_1 (
    .ALU_ctrl(alu_ctrl_extra_1_alu_ctrl3), .A(register_file_32_1_rdata1), .B(multiplexer_1_out),
    .R(alu_32_bits_1_r));  // open: C_out
endmodule

module ALU_ctrl_extra (
  input  I30,
  input  I14,
  input  I13,
  input  I12,
  input  I6,
  input  I5,
  input  I4,
  output ALU_ctrl3,
  output ALU_ctrl2,
  output ALU_ctrl1,
  output ALU_ctrl0,
  output ALU_Src
);

  wire and_3_out, and_4_out, and_5_out, and_6_out, and_7_out, not_1_out, not_2_out, not_3_out, not_4_out,
       not_5_out, not_6_out;

  not not_1 (not_1_out, I30);
  not not_2 (not_2_out, I14);
  not not_3 (not_3_out, I13);
  not not_4 (not_4_out, I12);
  not not_5 (not_5_out, I5);
  not not_6 (not_6_out, I4);
  and and_1 (ALU_ctrl3, not_3_out, I12);
  and and_2 (ALU_ctrl2, I30, not_3_out, not_4_out, I5);
  and and_3 (and_3_out, not_3_out, not_4_out);
  and and_4 (and_4_out, I30, not_3_out);
  and and_5 (and_5_out, not_2_out, not_4_out);
  and and_6 (and_6_out, I13, not_4_out);
  and and_7 (and_7_out, not_1_out, I14, not_3_out, I12);
  or or_1 (ALU_Src, not_5_out, not_6_out);
  or or_2 (ALU_ctrl1, and_3_out, not_6_out, and_4_out);
  or or_3 (ALU_ctrl0, and_5_out, and_6_out, and_7_out);
endmodule

module fetch_datapath (
);

  wire alu_ctrl_1_alu_ctrl0, alu_ctrl_1_alu_scr, and_1_out, clock_1_out, comparator_1_eq, control_1_branch,
       control_1_memread, control_1_memtoreg, control_1_memwrite, control_1_regwrite;
  wire [3:0] undriven;
  wire [7:0] register_1_q_2;
  wire [23:0] register_1_q;
  wire [31:0] adder_1_out, adder_2_out, alu_32_bits_1_r, datamemory_1_readdata, immgem_1_imm32,
       instructionmemory_1_instruction, multiplexer_1_out, multiplexer_2_out, multiplexer_3_out,
       register_file_32_1_rdata1, register_file_32_1_rdata2;

  Register #(.width(32)) register_1 (
    .D(multiplexer_2_out), .en(1'b1), .clk(clock_1_out), .Q({register_1_q_2, register_1_q}));  // open: clr
  Clock clock_1 (.out(clock_1_out));
  Adder #(.width(32)) adder_1 (.a({register_1_q_2, register_1_q}), .b(32'h4), .out(adder_1_out));  // open: cin, cout
  InstructionMemory instructionmemory_1 (
    .Address(register_1_q), .Clockin(clock_1_out), .Instruction(instructionmemory_1_instruction));
  ImmGem immgem_1 (.Instruction(instructionmemory_1_instruction), .IMM32(immgem_1_imm32));
  control control_1 (
    .I6_0(instructionmemory_1_instruction[6:0]), .MemtoReg(control_1_memtoreg),
    .RegWrite(control_1_regwrite), .MemRead(control_1_memread), .MemWrite(control_1_memwrite),
    .Branch(control_1_branch));
  register_file_32 register_file_32_1 (
    .WData(multiplexer_3_out), .RReg1(instructionmemory_1_instruction[19:15]), .Clock_in(clock_1_out),
    .Write(control_1_regwrite), .WReg(instructionmemory_1_instruction[11:7]),
    .RReg2(instructionmemory_1_instruction[24:20]), .RData1(register_file_32_1_rdata1),
    .RData2(register_file_32_1_rdata2));
  ALU_ctrl alu_ctrl_1 (
    .I30(instructionmemory_1_instruction[30]), .I14(instructionmemory_1_instruction[14]),
    .I13(instructionmemory_1_instruction[13]), .I12(instructionmemory_1_instruction[12]),
    .I6(instructionmemory_1_instruction[6]), .I5(instructionmemory_1_instruction[5]),
    .I4(instructionmemory_1_instruction[4]), .ALU_ctrl3(undriven[3]), .ALU_ctrl2(undriven[2]),
    .ALU_ctrl1(undriven[1]), .ALU_ctrl0(alu_ctrl_1_alu_ctrl0), .ALU_scr(alu_ctrl_1_alu_scr));
  Multiplexer #(.enable("false"), .width(32)) multiplexer_1 (
    .in0(register_file_32_1_rdata2), .in1(immgem_1_imm32), .out(multiplexer_1_out), .sel(alu_ctrl_1_alu_scr));
  Comparator #(.width(32)) comparator_1 (
    .a(register_file_32_1_rdata1), .b(register_file_32_1_rdata2), .eq(comparator_1_eq));  // open: gt, lt
  Adder #(.width(32)) adder_2 (
    .a({register_1_q_2, register_1_q}), .b(immgem_1_imm32), .out(adder_2_out));  // open: cin, cout
  ALU_32_bits alu_32_bits_1 (
    .ALU_ctrl(undriven), .A(register_file_32_1_rdata1), .B(multiplexer_1_out), .R(alu_32_bits_1_r));  // open: C_out
  Multiplexer #(.enable("false"), .width(32)) multiplexer_2 (
    .in0(adder_1_out), .in1(adder_2_out), .out(multiplexer_2_out), .sel(and_1_out));
  and and_1 (and_1_out, control_1_branch, comparator_1_eq);
  DataMemory datamemory_1 (
    .Address(alu_32_bits_1_r[25:0]), .MemWrite(control_1_memwrite), .MemRead(control_1_memread),
    .Clockin(clock_1_out), .WriteData(register_file_32_1_rdata2), .ReadData(datamemory_1_readdata));
  Multiplexer #(.enable("false"), .width(32)) multiplexer_3 (
    .in0(alu_32_bits_1_r), .in1(datamemory_1_readdata), .out(multiplexer_3_out), .sel(control_1_memtoreg));
endmodule

module control (
  input  [6:0] I6_0,
  output MemtoReg,
  output RegWrite,
  output MemRead,
  output MemWrite,
  output Branch
);

  wire not_1_out, not_2_out, not_3_out;

  not not_1 (not_1_out, I6_0[4]);
  not not_2 (not_2_out, I6_0[5]);
  not not_3 (not_3_out, I6_0[6]);
  and and_1 (MemtoReg, not_2_out, not_3_out);
  or or_1 (RegWrite, not_2_out, I6_0[6]);
  and and_2 (MemRead, not_2_out, not_3_out);
  and and_3 (MemWrite, not_1_out, I6_0[5], not_3_out);

  assign Branch = I6_0[4];
endmodule
